// Logisim project 15_bit_ALUmain.circ as structural Verilog: 11 circuits, main circuit main
module main (
  input  [1:0] Control,
  input  [14:0] A,
  input  [14:0] B,
  output [14:0] Result,
  output Zero,
  output Negative,
  output Overflow,
  output Carry
);

  L_15_bit_ALU_76185fa6 l_15_bit_alu_76185fa6_1 (
    .Control0(Control[0]), .Control1(Control[1]), .A(A), .Result(Result), .B(B), .Zero(Zero),
    .Negative(Negative), .Overflow(Overflow), .Carry(Carry));
endmodule

// 15-bit AND
module L_15_bit_and_bc268a4f (
  input  [14:0] A,
  input  [14:0] B,
  output [14:0] Result
);

  and and_1 (Result[0], A[0], B[0]);
  and and_2 (Result[1], A[1], B[1]);
  and and_3 (Result[2], A[2], B[2]);
  and and_4 (Result[3], A[3], B[3]);
  and and_5 (Result[4], A[4], B[4]);
  and and_6 (Result[5], A[5], B[5]);
  and and_7 (Result[6], A[6], B[6]);
  and and_8 (Result[7], A[7], B[7]);
  and and_9 (Result[8], A[8], B[8]);
  and and_10 (Result[9], A[9], B[9]);
  and and_11 (Result[10], A[10], B[10]);
  and and_12 (Result[11], A[11], B[11]);
  and and_13 (Result[12], A[12], B[12]);
  and and_14 (Result[13], A[13], B[13]);
  and and_15 (Result[14], A[14], B[14]);
endmodule

// 15-bit OR
module L_15_bit_OR_54dd5708 (
  input  [14:0] A,
  input  [14:0] B,
  output [14:0] Result
);

  or or_1 (Result[0], A[0], B[0]);
  or or_2 (Result[1], A[1], B[1]);
  or or_3 (Result[2], A[2], B[2]);
  or or_4 (Result[3], A[3], B[3]);
  or or_5 (Result[4], A[4], B[4]);
  or or_6 (Result[5], A[5], B[5]);
  or or_7 (Result[6], A[6], B[6]);
  or or_8 (Result[7], A[7], B[7]);
  or or_9 (Result[8], A[8], B[8]);
  or or_10 (Result[9], A[9], B[9]);
  or or_11 (Result[10], A[10], B[10]);
  or or_12 (Result[11], A[11], B[11]);
  or or_13 (Result[12], A[12], B[12]);
  or or_14 (Result[13], A[13], B[13]);
  or or_15 (Result[14], A[14], B[14]);
endmodule

module Full_adder (
  input  Carry_in_dd9ab7d0,
  input  A,
  input  B,
  output Result,
  output Carry_out_10543d98
);

  wire and_1_out, and_2_out, xor_1_out;

  and and_1 (and_1_out, B, A);
  xor xor_1 (xor_1_out, A, B);
  or or_1 (Carry_out_10543d98, and_1_out, and_2_out);
  and and_2 (and_2_out, xor_1_out, Carry_in_dd9ab7d0);
  xor xor_2 (Result, Carry_in_dd9ab7d0, xor_1_out);
endmodule

module L_15_bit_full_adder_6698948b (
  input  Carry_in_dd9ab7d0,
  input  A0,
  input  B0,
  input  A1,
  input  B1,
  input  A2,
  input  B2,
  input  A3,
  input  B3,
  input  A4,
  input  B4,
  input  A5,
  input  B5,
  input  A6,
  input  B6,
  input  A7,
  input  B7,
  input  A8,
  input  B8,
  input  A9,
  input  B9,
  input  A10,
  input  B10,
  input  A11,
  input  B11,
  input  A12,
  input  B12,
  input  A13,
  input  B13,
  input  A14,
  input  B14,
  output Result0,
  output Result1,
  output Result2,
  output Result3,
  output Result4,
  output Result5,
  output Result6,
  output Result7,
  output Result8,
  output Result9,
  output Result10,
  output Result11,
  output Result12,
  output Result13,
  output Result14,
  output Carry
);

  wire full_adder_1_carry_out_10543d98, full_adder_2_carry_out_10543d98, full_adder_3_carry_out_10543d98,
       full_adder_4_carry_out_10543d98, full_adder_5_carry_out_10543d98, full_adder_6_carry_out_10543d98,
       full_adder_7_carry_out_10543d98, full_adder_8_carry_out_10543d98, full_adder_9_carry_out_10543d98,
       full_adder_10_carry_out_10543d98, full_adder_11_carry_out_10543d98, full_adder_12_carry_out_10543d98,
       full_adder_13_carry_out_10543d98, full_adder_14_carry_out_10543d98;

  Full_adder full_adder_1 (
    .Carry_in_dd9ab7d0(Carry_in_dd9ab7d0), .A(A0), .Result(Result0), .B(B0),
    .Carry_out_10543d98(full_adder_1_carry_out_10543d98));
  Full_adder full_adder_2 (
    .Carry_in_dd9ab7d0(full_adder_1_carry_out_10543d98), .A(A1), .Result(Result1), .B(B1),
    .Carry_out_10543d98(full_adder_2_carry_out_10543d98));
  Full_adder full_adder_3 (
    .Carry_in_dd9ab7d0(full_adder_2_carry_out_10543d98), .A(A2), .Result(Result2), .B(B2),
    .Carry_out_10543d98(full_adder_3_carry_out_10543d98));
  Full_adder full_adder_4 (
    .Carry_in_dd9ab7d0(full_adder_3_carry_out_10543d98), .A(A3), .Result(Result3), .B(B3),
    .Carry_out_10543d98(full_adder_4_carry_out_10543d98));
  Full_adder full_adder_5 (
    .Carry_in_dd9ab7d0(full_adder_4_carry_out_10543d98), .A(A4), .Result(Result4), .B(B4),
    .Carry_out_10543d98(full_adder_5_carry_out_10543d98));
  Full_adder full_adder_6 (
    .Carry_in_dd9ab7d0(full_adder_5_carry_out_10543d98), .A(A5), .Result(Result5), .B(B5),
    .Carry_out_10543d98(full_adder_6_carry_out_10543d98));
  Full_adder full_adder_7 (
    .Carry_in_dd9ab7d0(full_adder_6_carry_out_10543d98), .A(A6), .Result(Result6), .B(B6),
    .Carry_out_10543d98(full_adder_7_carry_out_10543d98));
  Full_adder full_adder_8 (
    .Carry_in_dd9ab7d0(full_adder_7_carry_out_10543d98), .A(A7), .Result(Result7), .B(B7),
    .Carry_out_10543d98(full_adder_8_carry_out_10543d98));
  Full_adder full_adder_9 (
    .Carry_in_dd9ab7d0(full_adder_8_carry_out_10543d98), .A(A8), .Result(Result8), .B(B8),
    .Carry_out_10543d98(full_adder_9_carry_out_10543d98));
  Full_adder full_adder_10 (
    .Carry_in_dd9ab7d0(full_adder_9_carry_out_10543d98), .A(A9), .Result(Result9), .B(B9),
    .Carry_out_10543d98(full_adder_10_carry_out_10543d98));
  Full_adder full_adder_11 (
    .Carry_in_dd9ab7d0(full_adder_10_carry_out_10543d98), .A(A10), .Result(Result10), .B(B10),
    .Carry_out_10543d98(full_adder_11_carry_out_10543d98));
  Full_adder full_adder_12 (
    .Carry_in_dd9ab7d0(full_adder_11_carry_out_10543d98), .A(A11), .Result(Result11), .B(B11),
    .Carry_out_10543d98(full_adder_12_carry_out_10543d98));
  Full_adder full_adder_13 (
    .Carry_in_dd9ab7d0(full_adder_12_carry_out_10543d98), .A(A12), .Result(Result12), .B(B12),
    .Carry_out_10543d98(full_adder_13_carry_out_10543d98));
  Full_adder full_adder_14 (
    .Carry_in_dd9ab7d0(full_adder_13_carry_out_10543d98), .A(A13), .Result(Result13), .B(B13),
    .Carry_out_10543d98(full_adder_14_carry_out_10543d98));
  Full_adder full_adder_15 (
    .Carry_in_dd9ab7d0(full_adder_14_carry_out_10543d98), .A(A14), .Result(Result14), .B(B14),
    .Carry_out_10543d98(Carry));
endmodule

// FA
module L_15_bit_full_adder_concise_246bd7a0 (
  input  [14:0] A,
  input  Carry_in_dd9ab7d0,
  input  [14:0] B,
  output [14:0] Result,
  output Carry
);

  wire full_adder_1_carry_out_10543d98, full_adder_2_carry_out_10543d98, full_adder_3_carry_out_10543d98,
       full_adder_4_carry_out_10543d98, full_adder_5_carry_out_10543d98, full_adder_6_carry_out_10543d98,
       full_adder_7_carry_out_10543d98, full_adder_8_carry_out_10543d98, full_adder_9_carry_out_10543d98,
       full_adder_10_carry_out_10543d98, full_adder_11_carry_out_10543d98, full_adder_12_carry_out_10543d98,
       full_adder_13_carry_out_10543d98, full_adder_14_carry_out_10543d98;

  Full_adder full_adder_1 (
    .Carry_in_dd9ab7d0(Carry_in_dd9ab7d0), .A(A[0]), .Result(Result[0]), .B(B[0]),
    .Carry_out_10543d98(full_adder_1_carry_out_10543d98));
  Full_adder full_adder_2 (
    .Carry_in_dd9ab7d0(full_adder_1_carry_out_10543d98), .A(A[1]), .Result(Result[1]), .B(B[1]),
    .Carry_out_10543d98(full_adder_2_carry_out_10543d98));
  Full_adder full_adder_3 (
    .Carry_in_dd9ab7d0(full_adder_2_carry_out_10543d98), .A(A[2]), .Result(Result[2]), .B(B[2]),
    .Carry_out_10543d98(full_adder_3_carry_out_10543d98));
  Full_adder full_adder_4 (
    .Carry_in_dd9ab7d0(full_adder_3_carry_out_10543d98), .A(A[3]), .Result(Result[3]), .B(B[3]),
    .Carry_out_10543d98(full_adder_4_carry_out_10543d98));
  Full_adder full_adder_5 (
    .Carry_in_dd9ab7d0(full_adder_4_carry_out_10543d98), .A(A[4]), .Result(Result[4]), .B(B[4]),
    .Carry_out_10543d98(full_adder_5_carry_out_10543d98));
  Full_adder full_adder_6 (
    .Carry_in_dd9ab7d0(full_adder_5_carry_out_10543d98), .A(A[5]), .Result(Result[5]), .B(B[5]),
    .Carry_out_10543d98(full_adder_6_carry_out_10543d98));
  Full_adder full_adder_7 (
    .Carry_in_dd9ab7d0(full_adder_6_carry_out_10543d98), .A(A[6]), .Result(Result[6]), .B(B[6]),
    .Carry_out_10543d98(full_adder_7_carry_out_10543d98));
  Full_adder full_adder_8 (
    .Carry_in_dd9ab7d0(full_adder_7_carry_out_10543d98), .A(A[7]), .Result(Result[7]), .B(B[7]),
    .Carry_out_10543d98(full_adder_8_carry_out_10543d98));
  Full_adder full_adder_9 (
    .Carry_in_dd9ab7d0(full_adder_8_carry_out_10543d98), .A(A[8]), .Result(Result[8]), .B(B[8]),
    .Carry_out_10543d98(full_adder_9_carry_out_10543d98));
  Full_adder full_adder_10 (
    .Carry_in_dd9ab7d0(full_adder_9_carry_out_10543d98), .A(A[9]), .Result(Result[9]), .B(B[9]),
    .Carry_out_10543d98(full_adder_10_carry_out_10543d98));
  Full_adder full_adder_11 (
    .Carry_in_dd9ab7d0(full_adder_10_carry_out_10543d98), .A(A[10]), .Result(Result[10]), .B(B[10]),
    .Carry_out_10543d98(full_adder_11_carry_out_10543d98));
  Full_adder full_adder_12 (
    .Carry_in_dd9ab7d0(full_adder_11_carry_out_10543d98), .A(A[11]), .Result(Result[11]), .B(B[11]),
    .Carry_out_10543d98(full_adder_12_carry_out_10543d98));
  Full_adder full_adder_13 (
    .Carry_in_dd9ab7d0(full_adder_12_carry_out_10543d98), .A(A[12]), .Result(Result[12]), .B(B[12]),
    .Carry_out_10543d98(full_adder_13_carry_out_10543d98));
  Full_adder full_adder_14 (
    .Carry_in_dd9ab7d0(full_adder_13_carry_out_10543d98), .A(A[13]), .Result(Result[13]), .B(B[13]),
    .Carry_out_10543d98(full_adder_14_carry_out_10543d98));
  Full_adder full_adder_15 (
    .Carry_in_dd9ab7d0(full_adder_14_carry_out_10543d98), .A(A[14]), .Result(Result[14]), .B(B[14]),
    .Carry_out_10543d98(Carry));
endmodule

module L_15_bit_xor_8389f76f (
  input  in_1,
  input  [14:0] B,
  output [14:0] Result
);

  wire [14:0] bit_extender_1_out;

  assign bit_extender_1_out = {{14{in_1}}, in_1};  // Bit_Extender bit_extender_1
  xor xor_1 (Result[0], bit_extender_1_out[0], B[0]);
  xor xor_2 (Result[1], bit_extender_1_out[1], B[1]);
  xor xor_3 (Result[2], bit_extender_1_out[2], B[2]);
  xor xor_4 (Result[3], bit_extender_1_out[3], B[3]);
  xor xor_5 (Result[4], bit_extender_1_out[4], B[4]);
  xor xor_6 (Result[5], bit_extender_1_out[5], B[5]);
  xor xor_7 (Result[6], bit_extender_1_out[6], B[6]);
  xor xor_8 (Result[7], bit_extender_1_out[7], B[7]);
  xor xor_9 (Result[8], bit_extender_1_out[8], B[8]);
  xor xor_10 (Result[9], bit_extender_1_out[9], B[9]);
  xor xor_11 (Result[10], bit_extender_1_out[10], B[10]);
  xor xor_12 (Result[11], bit_extender_1_out[11], B[11]);
  xor xor_13 (Result[12], bit_extender_1_out[12], B[12]);
  xor xor_14 (Result[13], bit_extender_1_out[13], B[13]);
  xor xor_15 (Result[14], bit_extender_1_out[14], B[14]);
endmodule

// 15-bit \nADD/SUB
module Add_sub (
  input  Sub,
  input  [14:0] A,
  input  [14:0] B,
  output [14:0] Result,
  output Carry,
  output Overflow
);

  wire and_1_out, and_2_out, l_14th_bit_out_ba176a7e_1_l_14th_bit_209d214d,
       l_14th_bit_out_ba176a7e_2_l_14th_bit_209d214d, l_14th_bit_out_ba176a7e_3_l_14th_bit_209d214d,
       not_1_out, not_2_out, not_3_out;
  wire [14:0] l_15_bit_xor_8389f76f_1_result;

  L_14th_bit_out_ba176a7e l_14th_bit_out_ba176a7e_1 (
    .Input(A), .L_14th_bit_209d214d(l_14th_bit_out_ba176a7e_1_l_14th_bit_209d214d));
  not not_1 (not_1_out, l_14th_bit_out_ba176a7e_1_l_14th_bit_209d214d);
  L_14th_bit_out_ba176a7e l_14th_bit_out_ba176a7e_2 (
    .Input(B), .L_14th_bit_209d214d(l_14th_bit_out_ba176a7e_2_l_14th_bit_209d214d));
  not not_2 (not_2_out, l_14th_bit_out_ba176a7e_2_l_14th_bit_209d214d);
  L_15_bit_xor_8389f76f l_15_bit_xor_8389f76f_1 (.B(B), .Result(l_15_bit_xor_8389f76f_1_result), .in_1(Sub));
  L_15_bit_full_adder_concise_246bd7a0 l_15_bit_full_adder_concise_246bd7a0_1 (
    .Carry_in_dd9ab7d0(Sub), .A(A), .Result(Result), .B(l_15_bit_xor_8389f76f_1_result), .Carry(Carry));
  L_14th_bit_out_ba176a7e l_14th_bit_out_ba176a7e_3 (
    .Input(Result), .L_14th_bit_209d214d(l_14th_bit_out_ba176a7e_3_l_14th_bit_209d214d));
  not not_3 (not_3_out, l_14th_bit_out_ba176a7e_3_l_14th_bit_209d214d);
  and and_1 (and_1_out, not_3_out, l_14th_bit_out_ba176a7e_2_l_14th_bit_209d214d, l_14th_bit_out_ba176a7e_1_l_14th_bit_209d214d);
  and and_2 (and_2_out, l_14th_bit_out_ba176a7e_3_l_14th_bit_209d214d, not_2_out, not_1_out);
  or or_1 (Overflow, and_1_out, and_2_out);

  // Notes on the sheet:
  //   A31
  //   B31
  //   Result 31
endmodule

// 14th
module L_14th_bit_out_ba176a7e (
  input  [14:0] Input,
  output L_14th_bit_209d214d
);


  assign L_14th_bit_209d214d = Input[14];
endmodule

// Reduce-OR
module L_15_bit_reduce_or_3955d5b2 (
  input  [14:0] Input,
  output Output
);

  wire or_1_out, or_2_out, or_3_out, or_4_out, or_5_out, or_6_out, or_7_out, or_8_out, or_9_out, or_10_out,
       or_11_out, or_12_out, or_13_out;

  or or_1 (or_1_out, Input[0], Input[1]);
  or or_2 (or_2_out, or_1_out, Input[2]);
  or or_3 (or_3_out, or_2_out, Input[3]);
  or or_4 (or_4_out, or_3_out, Input[4]);
  or or_5 (or_5_out, or_4_out, Input[5]);
  or or_6 (or_6_out, or_5_out, Input[6]);
  or or_7 (or_7_out, or_6_out, Input[7]);
  or or_8 (or_8_out, or_7_out, Input[8]);
  or or_9 (or_9_out, or_8_out, Input[9]);
  or or_10 (or_10_out, or_9_out, Input[10]);
  or or_11 (or_11_out, or_10_out, Input[11]);
  or or_12 (or_12_out, or_11_out, Input[12]);
  or or_13 (or_13_out, or_12_out, Input[13]);
  or or_14 (Output, or_13_out, Input[14]);
endmodule

// 15-bit-ALU
module L_15_bit_ALU_76185fa6 (
  input  Control0,
  input  Control1,
  input  [14:0] A,
  input  [14:0] B,
  output [14:0] Result,
  output Zero,
  output Negative,
  output Overflow,
  output Carry
);

  wire l_15_bit_reduce_or_3955d5b2_1_output;
  wire [14:0] add_sub_1_result, l_15_bit_and_bc268a4f_1_result, l_15_bit_or_54dd5708_1_result,
       multiplexer_1_out;

  L_15_bit_and_bc268a4f l_15_bit_and_bc268a4f_1 (.A(A), .Result(l_15_bit_and_bc268a4f_1_result), .B(B));
  L_15_bit_OR_54dd5708 l_15_bit_or_54dd5708_1 (.A(A), .B(B), .Result(l_15_bit_or_54dd5708_1_result));
  Add_sub add_sub_1 (.Sub(Control0), .A(A), .Result(add_sub_1_result), .B(B), .Carry(Carry), .Overflow(Overflow));
  Multiplexer #(.width(15)) multiplexer_1 (
    .in0(l_15_bit_and_bc268a4f_1_result), .in1(l_15_bit_or_54dd5708_1_result), .out(multiplexer_1_out),
    .sel(Control0));  // open: en
  Multiplexer #(.width(15)) multiplexer_2 (
    .in0(multiplexer_1_out), .in1(add_sub_1_result), .out(Result), .sel(Control1));  // open: en
  L_14th_bit_out_ba176a7e l_14th_bit_out_ba176a7e_1 (.Input(Result), .L_14th_bit_209d214d(Negative));
  L_15_bit_reduce_or_3955d5b2 l_15_bit_reduce_or_3955d5b2_1 (
    .Input(Result), .Output(l_15_bit_reduce_or_3955d5b2_1_output));
  not not_1 (Zero, l_15_bit_reduce_or_3955d5b2_1_output);
endmodule
