// Logisim project CPU_demo_sir.circ as structural Verilog: 3 circuits, main circuit main
module main (
  input  [7:0] in_1
);

  wire clock_1_out, cpu_1_r, cpu_1_w, Reset_out;
  wire [3:0] cpu_1_addr;
  wire [7:0] cpu_1_dataout, ram_1_data;

  Clock clock_1 (.out(clock_1_out));
  Button Reset (.out(Reset_out));
  CPU cpu_1 (
    .Clk(clock_1_out), .Reset(Reset_out), .Input(in_1), .R(cpu_1_r), .W(cpu_1_w), .Addr(cpu_1_addr),
    .DataIn(ram_1_data), .DataOut(cpu_1_dataout));  // open: out_5
  RAM #(.addrWidth(4), .bus("separate")) ram_1 (
    .addr(cpu_1_addr), .din(cpu_1_dataout), .data(ram_1_data), .str(cpu_1_w), .clk(clock_1_out), .ld(cpu_1_r));  // open: sel, clr

  // Notes on the sheet:
  //   0 - AND
  //   1 - ADD
  //   2 - STO
  //   3 - OR
  //   4 - SUB
  //   5 - BUN
  //   6 - LDA
  //   7 - HLT
endmodule

module CPU (
  input  Clk,
  input  Reset,
  input  [7:0] DataIn,
  input  [7:0] Input,
  output [7:0] out_5,
  output R,
  output W,
  output [3:0] Addr,
  output [7:0] DataOut
);

  wire b1, c0, c1, controlunit_1_c1, controlunit_1_c2, d1, d2, LdA, LdA_from_MBR, LoadAc, LoadB, LoadIBR,
       LoadMAR, LoadOBR;
  wire [3:0] counter_1_q, multiplexer_1_out;
  wire [7:0] Ac, AcIn, ALUout, multiplexer_3_out;

  Multiplexer #(.width(4), .enable("false")) multiplexer_1 (
    .in0(counter_1_q), .in1(DataOut[3:0]), .out(multiplexer_1_out), .sel(d2));
  Multiplexer #(.width(8), .enable("false")) multiplexer_2 (
    .in0(ALUout), .in1(DataOut), .out(AcIn), .sel(LdA_from_MBR));
  Counter #(.width(4), .max('hf)) counter_1 (
    .load(controlunit_1_c2), .D(DataOut[3:0]), .count(controlunit_1_c1), .Q(counter_1_q), .clk(Clk),
    .clr(Reset));  // open: carry
  Register #(.width(4)) MAR (.D(multiplexer_1_out), .en(LoadMAR), .Q(Addr), .clk(Clk), .clr(Reset));
  Register #(.width(4)) IR (.D(DataOut[7:4]), .en(controlunit_1_c1), .clk(Clk), .clr(Reset));  // open: Q
  ControlUnit controlunit_1 (
    .IR(DataOut[7:4]), .Clk(Clk), .d1(d1), .c1(controlunit_1_c1), .R(R), .c2(controlunit_1_c2), .d2(d2),
    .b1(b1), .W(W), .b2(LoadIBR), .b3(LoadOBR), .LdAfrB(LdA_from_MBR), .Operation({c0, c1}), .LoadAc(LdA),
    .Reset(Reset));
  Multiplexer #(.width(8), .enable("false")) multiplexer_3 (.in0(DataIn), .in1(Ac), .out(multiplexer_3_out), .sel(b1));
  or or_1 (LoadMAR, d1, d2);
  Register MBR (.D(multiplexer_3_out), .en(LoadB), .Q(DataOut), .clk(Clk), .clr(Reset));
  Register u_Ac (.D(AcIn), .en(LoadAc), .Q(Ac), .clk(Clk), .clr(Reset));
  _8bitalu_main main_1 (
    .A(Ac), .B(DataOut), .Control0(c0), .Control1(c1), .Result(ALUout));  // open: Zero, Negative, Overflow, Carry
  or or_2 (LoadB, R, b1);
  or or_3 (LoadAc, LdA_from_MBR, LdA);
  Register IBR (.D(Input), .clk(Clk), .clr(Reset));  // open: en, Q
  Register OBR (.D(Ac), .en(LoadOBR), .Q(out_5), .clk(Clk), .clr(Reset));

  // Other names for the same wires on the sheet: clr = Reset; MBRout[7:0] = DataOut
endmodule

// CU
module ControlUnit (
  input  [3:0] IR,
  input  Clk,
  input  Reset,
  output d1,
  output c1,
  output R,
  output c2,
  output d2,
  output [1:0] Operation,
  output b1,
  output W,
  output b2,
  output LoadAc,
  output b3,
  output LdAfrB
);

  wire and_1_out, decoder_1_out6, decoder_1_out7, decoder_1_out8, decoder_1_out9, decoder_1_out15, not_1_out,
       or_1_out;
  wire [4:0] counter_1_q;
  wire [6:0] rom_1_data;

  Counter #(.width(5), .max('h1f)) counter_1 (
    .load(rom_1_data[2]), .D({IR[2:0], 2'b11}), .count(rom_1_data[0]), .Q(counter_1_q), .clk(and_1_out),
    .clr(or_1_out));  // open: carry
  or or_1 (or_1_out, rom_1_data[1], Reset);
  and and_1 (and_1_out, Clk, not_1_out);
  ROM #(.addrWidth(5), .dataWidth(7)) rom_1 (.addr(counter_1_q), .data(rom_1_data));  // open: sel
  not not_1 (not_1_out, decoder_1_out15);
  Decoder #(.select(4), .enable("false")) decoder_1 (
    .out1(d1), .out2(c1), .out3(R), .out4(c2), .out5(d2), .out6(decoder_1_out6), .out7(decoder_1_out7),
    .out8(decoder_1_out8), .out9(decoder_1_out9), .out10(b1), .out11(W), .out12(b2), .out13(b3),
    .out14(LdAfrB), .out15(decoder_1_out15), .sel(rom_1_data[6:3]));  // open: out0
  Priority_Encoder #(.select(2)) priority_encoder_1 (
    .in0(decoder_1_out6), .in1(decoder_1_out7), .in2(decoder_1_out8), .in3(decoder_1_out9), .out(Operation));  // open: gs, en_out, en_in
  or or_2 (LoadAc, decoder_1_out6, decoder_1_out7, decoder_1_out8, decoder_1_out9);

  // Notes on the sheet:
  //   contents of rom_1 (hex, n*v repeats v):
  //   9 19 14 29 19 31 2 29 19 39 2 29 51 59 2 29 19 41 2 29 19 49 2 21 2 2 2 29 19 71 2 78
endmodule
