// Logisim project cpu2307069.circ as structural Verilog: 3 circuits, main circuit main
module main (
  input  in_1,
  input  [14:0] Input,
  input  in_3,
  output [14:0] Output
);

  wire clock_1_out, cpu_1_r, cpu_1_rd, cpu_1_w, cpu_1_wd, reset;
  wire [7:0] cpu_1_addr;
  wire [14:0] Clatch_q, cpu_1_dataout, Dlatch_q, in, ram_1_data, ram_2_data;

  Clock clock_1 (.out(clock_1_out));
  Button u_Reset (.out(reset));
  CPU cpu_1 (
    .Clk(clock_1_out), .reset(reset), .Input(Input), .Output(Output), .DataOut(cpu_1_dataout), .R(cpu_1_r),
    .DataInput(in), .W(cpu_1_w), .Addr(cpu_1_addr), .RD(cpu_1_rd), .WD(cpu_1_wd));  // open: res2
  RAM #(.dataWidth(15), .bus("separate")) ram_1 (
    .addr(cpu_1_addr), .din(cpu_1_dataout), .data(ram_1_data), .str(cpu_1_w), .clk(clock_1_out),
    .ld(cpu_1_r), .clr(in_1));  // open: sel
  RAM #(.dataWidth(15), .bus("separate")) ram_2 (
    .addr(cpu_1_addr), .din(cpu_1_dataout), .data(ram_2_data), .str(cpu_1_wd), .clk(clock_1_out),
    .ld(cpu_1_rd), .clr(in_3));  // open: sel
  Register #(.width(15), .trigger("high")) Dlatch (
    .D(ram_2_data), .en(1'b1), .Q(Dlatch_q), .clk(clock_1_out), .clr(reset));
  Register #(.width(15), .trigger("high")) Clatch (
    .D(ram_1_data), .en(1'b1), .Q(Clatch_q), .clk(clock_1_out), .clr(reset));
  Multiplexer #(.width(15), .enable("false")) multiplexer_1 (.in0(Clatch_q), .in1(Dlatch_q), .out(in), .sel(cpu_1_rd));

  // Notes on the sheet:
  //   0 - AND
  //   1 - ADD
  //   2 - STO
  //   3 - OR
  //   4 - SUB
  //   5 - BUN
  //   6 - LDA
  //   7 - HLT
  //   NOP-04
  //   LOAD-05
  //   STORE-08
  //   ADD-0b
  //   SUB-0f
  //   OR-13
  //   HLT-34
  //   AND-17
  //   MUL-21
  //   IN-24
  //   INM-26
  //   PUSH-2c
  //   jmp-35
  //   JMP-21
  //   OUT-25
  //   OUTM-29
  //   POP-30
endmodule

module CPU (
  input  [14:0] DataInput,
  input  Clk,
  input  reset,
  input  [14:0] Input,
  output [14:0] Output,
  output [14:0] DataOut,
  output R,
  output W,
  output [7:0] Addr,
  output RD,
  output [14:0] res2,
  output WD
);

  wire a1, a2, a3, a4, AC_ALUout, ac_ibr, ac_mbr, ac_mulresult, and_1_out, and_2_out, c0, c1, incpc, ir,
       LoadB, LoadMAR, main_1_zero, mar_ir, mar_pc, mar_sp, mbr_ac, mbr_ibr, muldone, multiplexer_2_out,
       negative, Negative_Flag, obr_ac, obr_mbr, or_1_out, or_3_out, or_5_out, or_6_out, pc_mbr,
       pc_mbr_if_Z___1, pop_help, push_help, sp_1, sp_1_t, strt_mul, Zflag;
  wire [7:0] IRout, m1_t, MARin, multiplexer_1_out, PC_q, sp;
  wire [14:0] AcIn, acout, ALUout, booth_s_multiplier_1_res2, IBRout, M1, main_1_result, MBRin, mulRes,
       multiplexer_7_out, multiplexer_8_out, multiplexer_9_out;
  wire [14:8] IR_q;

  Multiplexer #(.width(8), .enable("false")) multiplexer_1 (
    .in0(PC_q), .in1(DataOut[7:0]), .out(multiplexer_1_out), .sel(mar_ir));
  Multiplexer #(.enable("false")) multiplexer_2 (
    .in0(pc_mbr), .in1(or_1_out), .out(multiplexer_2_out), .sel(pc_mbr_if_Z___1));
  or or_1 (or_1_out, pc_mbr, Zflag);
  Multiplexer #(.width(8), .enable("false")) multiplexer_3 (
    .in0(multiplexer_1_out), .in1(sp), .out(m1_t), .sel(mar_sp));
  Multiplexer #(.width(8), .enable("false")) multiplexer_4 (.in0(m1_t), .in1(IRout), .out(MARin), .sel(mar_ir));
  Counter PC (
    .load(multiplexer_2_out), .D(DataOut[7:0]), .count(incpc), .Q(PC_q), .clk(Clk), .clr(reset));  // open: carry
  Register MAR (.D(MARin), .en(LoadMAR), .Q(Addr), .clk(Clk), .clr(reset));
  Register #(.width(15)) u_IR (.D(DataOut), .en(ir), .Q({IR_q, IRout}), .clk(Clk), .clr(reset));
  ControlUnit controlunit_1 (
    .out_6(mar_pc), .out_7(incpc), .out_8(R), .out_9(ir), ._5(mar_ir), .out_11(ac_mbr), .out_12(W),
    .out_13(a1), .out_14(a2), ._10(a3), .out_16(a4), .out_17(mbr_ac), .out_18(sp_1_t), .out_19(sp_1),
    ._15(mar_sp), .out_21(strt_mul), .out_22(ac_mulresult), ._20(AC_ALUout), .out_26(RD), .out_27(WD),
    .out_28(pc_mbr_if_Z___1), .out_29(pc_mbr), ._25(ac_ibr), .out_31(obr_ac), .out_32(mbr_ibr),
    .out_33(obr_mbr), .out_34(push_help), ._30(pop_help), .rst(reset), .ADDR(DataOut[13:8]), .Clk(Clk),
    .muldone(muldone));  // open: _0, out_23, out_24, out_36
  Multiplexer #(.width(15), .enable("false")) multiplexer_5 (.in0(DataInput), .in1(acout), .out(M1), .sel(mbr_ac));
  or or_2 (LoadMAR, mar_pc, mar_sp, mar_ir);
  Register #(.width(15)) MBR (.D(MBRin), .en(LoadB), .Q(DataOut), .clk(Clk), .clr(reset));
  Register #(.width(15)) Ac (.D(AcIn), .en(or_3_out), .Q(acout), .clk(Clk), .clr(reset));
  or or_3 (or_3_out, ac_ibr, AC_ALUout, ac_mbr, ac_mulresult);
  Multiplexer #(.width(15), .enable("false")) multiplexer_6 (.in0(M1), .in1(IBRout), .out(MBRin), .sel(mbr_ibr));
  or or_4 (LoadB, RD, R, mbr_ac, mbr_ibr);
  Multiplexer #(.width(15), .enable("false")) multiplexer_7 (
    .in0(acout), .in1(DataOut), .out(multiplexer_7_out), .sel(obr_mbr));
  Register #(.width(15), .trigger("high")) IBR (.D(Input), .en(1'b1), .Q(IBRout), .clk(Clk), .clr(reset));
  Register #(.width(15)) OBR (.D(multiplexer_7_out), .en(or_5_out), .Q(Output), .clk(Clk), .clr(reset));
  or or_5 (or_5_out, obr_mbr, obr_ac);
  Multiplexer #(.width(15), .enable("false")) multiplexer_8 (
    .in0(ALUout), .in1(DataOut), .out(multiplexer_8_out), .sel(ac_mbr));
  and and_1 (and_1_out, Clk, strt_mul);
  Priority_Encoder #(.select(2)) priority_encoder_1 (
    .in0(a1), .in1(a2), .in2(a3), .in3(a4), .out({c1, c0}));  // open: gs, en_out, en_in
  or or_6 (or_6_out, sp_1_t, sp_1);
  _15_bit_ALU_main main_1 (
    .A(acout), .B(DataOut), .Control0(c0), .control1(c1), .Result(main_1_result), .Zero(main_1_zero));  // open: Negative, Overflow, Carry
  Multiplexer #(.width(15), .enable("false")) multiplexer_9 (
    .in0(multiplexer_8_out), .in1(IBRout), .out(multiplexer_9_out), .sel(ac_ibr));
  Multiplexer #(.width(15), .enable("false")) multiplexer_10 (
    .in0(multiplexer_9_out), .in1(mulRes), .out(AcIn), .sel(ac_mulresult));
  Booth_s_multiplier booth_s_multiplier_1 (
    .M_input(acout), .Q_input(DataOut), .clk(and_1_out), .done(muldone), .res2(booth_s_multiplier_1_res2),
    .res1(res2));  // open: Reset
  Counter #(.trigger("falling")) u_sp (
    .load(sp_1_t), .count(or_6_out), .Q(sp), .clk(and_2_out), .clr(reset));  // open: D, carry
  and and_2 (and_2_out, or_6_out, Clk);
  Register #(.width(15)) u_ALUout (.D(main_1_result), .en(1'b1), .Q(ALUout), .clk(Clk), .clr(reset));
  Register #(.width(15)) u_mulRes (.D(booth_s_multiplier_1_res2), .en(1'b1), .Q(mulRes), .clk(Clk));  // open: clr
  D_Flip_Flop d_ff_1 (.clk(Clk), .D(main_1_zero), .Q(Zflag));  // open: Qn, preset, en, reset
  D_Flip_Flop d_ff_2 (.clk(Clk), .D(negative), .Q(Negative_Flag));  // open: Qn, preset, en, reset

  // Other names for the same wires on the sheet: clr = reset; encoder_out[1:0] = {c1, c0}; MBRout[14:0] = DataOut;
  //   aaa[5:0] = DataOut[13:8]
endmodule

// 0x3ff
module ControlUnit (
  input  muldone,
  input  [5:0] ADDR,
  input  Clk,
  input  rst,
  output _0,
  output out_6,
  output out_7,
  output out_8,
  output out_9,
  output _5,
  output out_11,
  output out_12,
  output out_13,
  output out_14,
  output _10,
  output out_16,
  output out_17,
  output out_18,
  output out_19,
  output _15,
  output out_21,
  output out_22,
  output out_23,
  output out_24,
  output _20,
  output out_26,
  output out_27,
  output out_28,
  output out_29,
  output _25,
  output out_31,
  output out_32,
  output out_33,
  output out_34,
  output _30,
  output out_36
);

  wire and_1_out, d_ff_1_q, not_1_out, or_1_out, or_2_out;
  wire [5:0] counter_1_q;
  wire [7:0] rom_1_data;

  Counter #(.width(6), .max('h3f), .ongoal("continue")) counter_1 (
    .load(rom_1_data[2]), .D(ADDR), .count(or_1_out), .Q(counter_1_q), .clk(and_1_out), .clr(or_2_out));  // open: carry
  and and_1 (and_1_out, Clk, not_1_out);
  or or_1 (or_1_out, muldone, rom_1_data[0]);
  or or_2 (or_2_out, d_ff_1_q, rst);
  ROM #(.addrWidth(6)) rom_1 (.addr(counter_1_q), .data(rom_1_data));  // open: sel
  D_Flip_Flop d_ff_1 (.clk(and_1_out), .D(rom_1_data[1]), .Q(d_ff_1_q));  // open: Qn, preset, en, reset
  not not_1 (not_1_out, out_36);
  Decoder #(.select(5), .enable("false")) decoder_1 (
    .out0(_0), .out1(out_6), .out2(out_7), .out3(out_8), .out4(out_9), .out5(_5), .out6(out_11),
    .out7(out_12), .out8(out_13), .out9(out_14), .out10(_10), .out11(out_16), .out12(out_17), .out13(out_18),
    .out14(out_19), .out15(_15), .out16(out_21), .out17(out_22), .out18(out_23), .out19(out_24), .out20(_20),
    .out21(out_26), .out22(out_27), .out23(out_28), .out24(out_29), .out25(_25), .out26(out_31),
    .out27(out_32), .out28(out_33), .out29(out_34), .out30(_30), .out31(out_36), .sel(rom_1_data[7:3]));

  // Notes on the sheet:
  //   contents of rom_1 (hex, n*v repeats v):
  //   9 11 19 24 2 29 a9 32 29 61 b2 29 a9 51 a2 29 a9 59 a2 29 a9 49 a2 29 a9 41 a2 29 a9 80 8a 29 a9 91
  //   9a 29 a9 c2 ca d2 d9 29 b2 29 a9 e2 69 79 61 b2 79 a9 31 72 fa ba
endmodule
